// Logisim project Hamming.circ as structural Verilog: 4 circuits, main circuit CIRCUITO
module CIRCUITO (
  input  in_1,
  input  in_2,
  input  in_3,
  input  in_4,
  input  in_5,
  input  in_6,
  input  in_7,
  input  in_8,
  input  in_9,
  input  in_10,
  input  in_11,
  output out_12,
  output out_13,
  output out_14,
  output out_15,
  output out_16
);

  wire deco_bin_dec_1__3, deco_bin_dec_1__5, deco_bin_dec_1__6, deco_bin_dec_1__7, gen_err_1_out_18,
       gen_err_1_out_19, gen_err_1_out_20, gen_err_1_out_21, gen_err_1_out_22, gen_err_1_out_23,
       gen_err_1_out_24, hamming_1_out_5, hamming_1_out_6, hamming_1_out_7, hamming_1_out_8, hamming_1_out_9,
       hamming_1_out_10, hamming_1_out_11, hamming_2_out_5, hamming_2_out_6, hamming_2_out_7,
       hamming_2_out_8, hamming_2_out_9, hamming_2_out_10, hamming_2_out_11, xor_1_out, xor_2_out, xor_3_out;

  HAMMING hamming_1 (
    .in_1(in_1), .in_2(in_2), .in_3(in_3), .in_4(in_4), .out_5(hamming_1_out_5), .out_6(hamming_1_out_6),
    .out_7(hamming_1_out_7), .out_8(hamming_1_out_8), .out_9(hamming_1_out_9), .out_10(hamming_1_out_10),
    .out_11(hamming_1_out_11));
  GEN_ERR gen_err_1 (
    .in_2(hamming_1_out_5), .in_3(hamming_1_out_6), .in_4(hamming_1_out_7), .in_5(hamming_1_out_8),
    .in_6(hamming_1_out_9), .in_7(hamming_1_out_10), .in_8(hamming_1_out_11), .out_18(gen_err_1_out_18),
    .out_19(gen_err_1_out_19), .out_20(gen_err_1_out_20), .out_21(gen_err_1_out_21),
    .out_22(gen_err_1_out_22), .out_23(gen_err_1_out_23), .out_24(gen_err_1_out_24), .in_15(in_5),
    .in_14(in_6), .in_13(in_7), .in_12(in_8), .in_11(in_9), .in_10(in_10), .in_9(in_11));  // open: in_16, in_1, out_17
  HAMMING hamming_2 (
    .in_1(gen_err_1_out_20), .in_2(gen_err_1_out_22), .in_3(gen_err_1_out_23), .in_4(gen_err_1_out_24),
    .out_5(hamming_2_out_5), .out_6(hamming_2_out_6), .out_7(hamming_2_out_7), .out_8(hamming_2_out_8),
    .out_9(hamming_2_out_9), .out_10(hamming_2_out_10), .out_11(hamming_2_out_11));
  xor xor_1 (xor_1_out, gen_err_1_out_18, hamming_2_out_5);
  xor xor_2 (xor_2_out, gen_err_1_out_19, hamming_2_out_6);
  xor xor_3 (xor_3_out, gen_err_1_out_21, hamming_2_out_8);
  or or_1 (out_12, xor_3_out, xor_2_out, xor_1_out);
  DECO_BIN_DEC deco_bin_dec_1 (
    .a(xor_1_out), .b(xor_2_out), .c(xor_3_out), ._3(deco_bin_dec_1__3), ._5(deco_bin_dec_1__5),
    ._6(deco_bin_dec_1__6), ._7(deco_bin_dec_1__7));  // open: _0, _1, _2, _4
  xor xor_4 (out_13, deco_bin_dec_1__3, hamming_2_out_7);
  xor xor_5 (out_14, deco_bin_dec_1__5, hamming_2_out_9);
  xor xor_6 (out_15, deco_bin_dec_1__6, hamming_2_out_10);
  xor xor_7 (out_16, deco_bin_dec_1__7, hamming_2_out_11);

  // Notes on the sheet:
  //   HAMMING
  //   HAMMING
  //   DECO BIN/DEC
endmodule

module GEN_ERR (
  input  in_1,
  input  in_2,
  input  in_3,
  input  in_4,
  input  in_5,
  input  in_6,
  input  in_7,
  input  in_8,
  input  in_9,
  input  in_10,
  input  in_11,
  input  in_12,
  input  in_13,
  input  in_14,
  input  in_15,
  input  in_16,
  output out_17,
  output out_18,
  output out_19,
  output out_20,
  output out_21,
  output out_22,
  output out_23,
  output out_24
);

  xor xor_1 (out_24, in_8, in_9);
  xor xor_2 (out_23, in_7, in_10);
  xor xor_3 (out_22, in_6, in_11);
  xor xor_4 (out_21, in_5, in_12);
  xor xor_5 (out_20, in_4, in_13);
  xor xor_6 (out_19, in_3, in_14);
  xor xor_7 (out_18, in_2, in_15);
  xor xor_8 (out_17, in_1, in_16);
endmodule

module HAMMING (
  input  in_1,
  input  in_2,
  input  in_3,
  input  in_4,
  output out_5,
  output out_6,
  output out_7,
  output out_8,
  output out_9,
  output out_10,
  output out_11
);

  wire xor_1_out, xor_2_out, xor_3_out;

  xor xor_1 (xor_1_out, in_1, in_2);
  xor xor_2 (xor_2_out, in_1, in_3);
  xor xor_3 (xor_3_out, in_2, in_3);
  xor xor_4 (out_5, xor_1_out, in_4);
  xor xor_5 (out_8, xor_3_out, in_4);
  xor xor_6 (out_6, xor_2_out, in_4);

  assign out_7 = in_1;
  assign out_9 = in_2;
  assign out_10 = in_3;
  assign out_11 = in_4;
endmodule

module DECO_BIN_DEC (
  input  a,
  input  b,
  input  c,
  output _0,
  output _1,
  output _2,
  output _3,
  output _4,
  output _5,
  output _6,
  output _7
);

  wire not_1_out, not_2_out, not_3_out;

  not not_1 (not_1_out, a);
  not not_2 (not_2_out, b);
  not not_3 (not_3_out, c);
  and and_1 (_0, not_1_out, not_2_out, not_3_out);
  and and_2 (_1, a, not_2_out, not_3_out);
  and and_3 (_2, not_1_out, b, not_3_out);
  and and_4 (_3, a, b, not_3_out);
  and and_5 (_4, not_1_out, not_2_out, c);
  and and_6 (_5, a, not_2_out, c);
  and and_7 (_6, not_1_out, b, c);
  and and_8 (_7, a, b, c);
endmodule
